# Fritzing sketch arco-fritzing-new (saved by Fritzing 0.9.3b)
breadboards: 1

parts:
  SparkFun_5-Way_Tactile_Switch1 = SparkFun 5-Way Tactile Switch Breakout
  OLED_I2C1 = OLED 128x64 I2C Monochrome Display
  S1 = Tactile Switch Buttons - 12mm Square [package=tactile-pth-12mm]
  S2 = Tactile Switch Buttons - 12mm Square [package=tactile-pth-12mm]
  Part1 = Arduino Uno (Rev3)
  J2 = Piezo Speaker

nets:
  GND: SparkFun_5-Way_Tactile_Switch1.GND, OLED_I2C1.GND, S1.1, S1.3, S2.1, S2.3, Part1.GND, J2.pin1
  N1: SparkFun_5-Way_Tactile_Switch1.RIGHT, Part1.D12/MISO
  N2: SparkFun_5-Way_Tactile_Switch1.DOWN, Part1.D11_PWM/MOSI
  N3: SparkFun_5-Way_Tactile_Switch1.LEFT, Part1.D10_PWM/SS
  N4: SparkFun_5-Way_Tactile_Switch1.CENTER, Part1.D9_PWM
  N5: SparkFun_5-Way_Tactile_Switch1.UP, Part1.D8
  VCC: SparkFun_5-Way_Tactile_Switch1.VCC, OLED_I2C1.VDD, Part1.5V
  N6: OLED_I2C1.SDA, Part1.A4/SDA
  N7: OLED_I2C1.SCK, Part1.A5/SCL
  N8: S1.2, S1.4, Part1.D3_PWM
  N9: S2.2, S2.4, Part1.D2
  N10: Part1.D13/SCK, J2.pin2

custom parts:
  SparkFun 5-Way Tactile Switch Breakout: The SparkFun 5-Way Tactile Switch Breakout. The board contains a 5-way directional input device (up, down, left, right, and center click).
  Tactile Switch Buttons - 12mm Square: Medium-sized clicky momentary switches are standard input "buttons" on electronic projects. These work best in a PCB but can be used on a solderless breadboard as shown in this tutorial. The pins are normally open (disconnected) and when the button is pressed they are momentarily closed. They come in a pack of 10, they're pretty handy so you'll want to keep them around. You can find an EAGLE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
