# Fritzing sketch sketch1 (saved by Fritzing 0.9.3b)
circuit board: 8.46667cm x 5.64444cm
breadboards: 3

parts:
  Součástka1 = Arduino Nano (Rev3.0)
  S1 = Pushbutton [package="[THT]"]
  S2 = Pushbutton [package="[THT]"]
  OLED_I2C1 = OLED 128x64 I2C Monochrome Display
  SparkFun_5-Way_Tactile_Switch1 = SparkFun 5-Way Tactile Switch Breakout
  VCC1 = Battery  # not connected

nets:
  GND: Součástka1.GND, OLED_I2C1.GND, SparkFun_5-Way_Tactile_Switch1.GND
  N1: Součástka1.D2, SparkFun_5-Way_Tactile_Switch1.LEFT
  N2: Součástka1.D3, SparkFun_5-Way_Tactile_Switch1.UP
  N3: Součástka1.D4, SparkFun_5-Way_Tactile_Switch1.RIGHT
  N4: Součástka1.D5, SparkFun_5-Way_Tactile_Switch1.CENTER
  N5: Součástka1.D6, SparkFun_5-Way_Tactile_Switch1.DOWN
  3V3: Součástka1.3V3, OLED_I2C1.VDD, SparkFun_5-Way_Tactile_Switch1.VCC
  N6: S1.Pin_1, S1.Pin_2
  N7: S1.Pin_3, S1.Pin_4
  N8: S2.Pin_1, S2.Pin_2
  N9: S2.Pin_3, S2.Pin_4

custom parts:
  SparkFun 5-Way Tactile Switch Breakout: The SparkFun 5-Way Tactile Switch Breakout. The board contains a 5-way directional input device (up, down, left, right, and center click).
