# Fritzing sketch arco-fritzing (saved by Fritzing 0.9.3b)
breadboards: 1

parts:
  Part1 = Arduino Uno (Rev3) - ICSP
  OLED_I2C1 = OLED 128x64 I2C Monochrome Display
  J1 = Piezo Speaker
  S1 = Tactile Switch Buttons - 12mm Square [package=tactile-pth-12mm]
  S2 = Tactile Switch Buttons - 12mm Square [package=tactile-pth-12mm]
  SparkFun_5-Way_Tactile_Switch1 = SparkFun 5-Way Tactile Switch Breakout

nets:
  N1: Part1.D8, SparkFun_5-Way_Tactile_Switch1.UP
  N2: Part1.D9_PWM, SparkFun_5-Way_Tactile_Switch1.CENTER
  N3: Part1.D10_PWM/SS, SparkFun_5-Way_Tactile_Switch1.LEFT
  N4: Part1.D11_PWM/MOSI, SparkFun_5-Way_Tactile_Switch1.DOWN
  N5: Part1.D12/MISO, SparkFun_5-Way_Tactile_Switch1.RIGHT
  N6: Part1.D13/SCK, J1.pin2
  GND: Part1.GND, OLED_I2C1.GND, J1.pin1, S1.1, S1.3, S2.1, S2.3, SparkFun_5-Way_Tactile_Switch1.GND
  N7: Part1.A4/SDA, OLED_I2C1.SDA
  N8: Part1.A5/SCL, OLED_I2C1.SCK
  N9: Part1.D2, S1.2, S1.4
  N10: Part1.D3_PWM, S2.2, S2.4
  3V3: Part1.3V3, SparkFun_5-Way_Tactile_Switch1.VCC
  5V: Part1.5V, OLED_I2C1.VDD

custom parts:
  Tactile Switch Buttons - 12mm Square: Medium-sized clicky momentary switches are standard input "buttons" on electronic projects. These work best in a PCB but can be used on a solderless breadboard as shown in this tutorial. The pins are normally open (disconnected) and when the button is pressed they are momentarily closed. They come in a pack of 10, they're pretty handy so you'll want to keep them around. You can find an EAGLE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
  SparkFun 5-Way Tactile Switch Breakout: The SparkFun 5-Way Tactile Switch Breakout. The board contains a 5-way directional input device (up, down, left, right, and center click).
