# Fritzing sketch sketch2 (saved by Fritzing 0.9.3b)
circuit board: 8cm x 10cm
breadboards: 3

parts:
  nano = Arduino Nano (Rev3.0)
  5-Way = SparkFun 5-Way Tactile Switch Breakout
  dc/dc_booster = mystery part, 12 pins [chip_label="dc/dc booster"]
  S2 = Tactile Switch Buttons - 12mm Square [package=tactile-pth-12mm]
  S1 = Tactile Switch Buttons - 12mm Square [package=tactile-pth-12mm]
  U1 = SWITCH_SPDT [package=kps-1290]
  oled = mystery part, 4 pins [chip_label=oled]
  buzzer = mystery part, 3 pins [chip_label=buzzer]
  R2 = Resistor [tolerance=±5% resistance=220 package=THT]
  R1 = Resistor [tolerance=±5% resistance=220 package=THT]

nets:
  GND: nano.GND, 5-Way.GND, dc/dc_booster.pin5, oled.pin1, buzzer.pin3, R2.Pin_1, R1.Pin_1
  N1: nano.D2, 5-Way.UP
  N2: nano.D3, 5-Way.CENTER
  N3: nano.D4, 5-Way.LEFT
  N4: nano.D5, 5-Way.DOWN
  N5: nano.D6, 5-Way.RIGHT
  N6: nano.D11/MOSI, buzzer.pin1
  N7: nano.D12/MISO, S1.1, S1.3, R2.Pin_0
  N8: nano.5V, dc/dc_booster.pin2, oled.pin2, buzzer.pin2
  N9: nano.A5, oled.pin3
  N10: nano.A4, oled.pin4
  3V3: nano.3V3, 5-Way.VCC, S2.2, S2.4, S1.2, S1.4
  N11: nano.D13/SCK, S2.1, S2.3, R1.Pin_0
  N12: dc/dc_booster.pin12, U1.S

notes:
  DIY-Arduino-Handheld-Game-Console

custom parts:
  SparkFun 5-Way Tactile Switch Breakout: The SparkFun 5-Way Tactile Switch Breakout. The board contains a 5-way directional input device (up, down, left, right, and center click).
  Tactile Switch Buttons - 12mm Square: Medium-sized clicky momentary switches are standard input "buttons" on electronic projects. These work best in a PCB but can be used on a solderless breadboard as shown in this tutorial. The pins are normally open (disconnected) and when the button is pressed they are momentarily closed. They come in a pack of 10, they're pretty handy so you'll want to keep them around. You can find an EAGLE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
