# Fritzing sketch sketch3 (saved by Fritzing 0.9.3b)
circuit board: 8cm x 10cm
breadboards: 2

parts:
  nano1 = Arduino Nano (Rev3.0)
  5-Way = SparkFun 5-Way Tactile Switch Breakout
  oled1 = mystery part, 4 pins [chip_label=oled]
  RS = Resistor [tolerance=±5% resistance=10k package=THT]
  RA = Resistor [tolerance=±5% resistance=10k package=THT]
  buzzer1 = mystery part, 3 pins [chip_label=buzzer]
  dc/dc_booster1 = mystery part, 12 pins [chip_label="dc/dc booster"]
  U2 = SWITCH_SPDT [package=kps-1290]
  action = mystery part, 6 pins [chip_label=action]
  start = mystery part, 6 pins [chip_label=start]

nets:
  N1: nano1.GND, dc/dc_booster1.pin5
  N2: nano1.D2, 5-Way.UP
  N3: nano1.D3, 5-Way.CENTER
  N4: nano1.D4, 5-Way.LEFT
  N5: nano1.D5, 5-Way.DOWN
  N6: nano1.D6, 5-Way.RIGHT
  N7: nano1.D11/MOSI, buzzer1.pin1
  N8: nano1.D12/MISO, RA.Pin_1, action.pin4
  N9: nano1.5V, dc/dc_booster1.pin2
  N10: nano1.A5, oled1.pin3
  N11: nano1.A4, oled1.pin4
  N12: nano1.D13/SCK, RS.Pin_1, start.pin4
  N13: 5-Way.GND, oled1.pin1, RS.Pin_0, RA.Pin_0, buzzer1.pin3
  N14: 5-Way.VCC, oled1.pin2, buzzer1.pin2, action.pin6, start.pin6
  N15: dc/dc_booster1.pin12, U2.S

notes:
  DIY-Arduino-Handheld-Game-Console

custom parts:
  SparkFun 5-Way Tactile Switch Breakout: The SparkFun 5-Way Tactile Switch Breakout. The board contains a 5-way directional input device (up, down, left, right, and center click).
