# Fritzing sketch sketch1 (saved by Fritzing 0.9.3b)
circuit board: 8.46667cm x 5.64444cm
breadboards: 3

parts:
  Součástka1 = Arduino Nano (Rev3.0)
  S1 = Pushbutton [package="[THT]"]
  S2 = Pushbutton [package="[THT]"]
  OLED_I2C1 = OLED 128x64 I2C Monochrome Display
  SparkFun_5-Way_Tactile_Switch1 = SparkFun 5-Way Tactile Switch Breakout
  VCC1 = Battery  # not connected
  U1 = mystery part, 3 pins [chip_label="mystery buzzer"]
  R1 = Resistor [tolerance=±5% resistance=220 package=THT]
  R2 = Resistor [tolerance=±5% resistance=220 package=THT]

nets:
  GND: Součástka1.GND, OLED_I2C1.GND, SparkFun_5-Way_Tactile_Switch1.GND, U1.pin3, R1.Pin_1, R2.Pin_1
  N1: Součástka1.D2, SparkFun_5-Way_Tactile_Switch1.UP
  N2: Součástka1.D3, SparkFun_5-Way_Tactile_Switch1.CENTER
  N3: Součástka1.D4, SparkFun_5-Way_Tactile_Switch1.LEFT
  N4: Součástka1.D5, SparkFun_5-Way_Tactile_Switch1.DOWN
  N5: Součástka1.D6, SparkFun_5-Way_Tactile_Switch1.RIGHT
  N6: Součástka1.D11/MOSI, U1.pin1
  N7: Součástka1.D12/MISO, S2.Pin_3, S2.Pin_4, R2.Pin_0
  N8: Součástka1.5V, U1.pin2
  N9: Součástka1.A5, OLED_I2C1.SCK
  N10: Součástka1.A4, OLED_I2C1.SDA
  3V3: Součástka1.3V3, S1.Pin_1, S1.Pin_2, S2.Pin_1, S2.Pin_2, OLED_I2C1.VDD, SparkFun_5-Way_Tactile_Switch1.VCC
  N11: Součástka1.D13/SCK, S1.Pin_3, S1.Pin_4, R1.Pin_0

custom parts:
  SparkFun 5-Way Tactile Switch Breakout: The SparkFun 5-Way Tactile Switch Breakout. The board contains a 5-way directional input device (up, down, left, right, and center click).
